# Fritzing sketch hw (saved by Fritzing 0.9.0b)
circuit board: 8.46667cm x 5.64444cm
breadboards: 1

parts:
  Part1 = Arduino Uno (Rev3)
  Part2 = Arduino Uno (Rev3)
  U1 = Voltage Regulator - 5V [package="TO220 [THT]"]
  R1 = Resistor [tolerance=±5% resistance=4.7 package="0603 [SMD]"]
  DS2 = DS18B20 1-Wire Temperature Sensor [part_number=DS18B20]
  DS3 = DS18B20 1-Wire Temperature Sensor [part_number=DS18B20]
  S1 = Toggle Switch [package=THT]
  J1 = Power Jack [package=power_jack_combo]
  U3 = Graphical LCD 128x64 [package=lcd-g12864]
  S2 = Momentary Switch [package=tactile-pth]
  S3 = Momentary Switch [package=tactile-pth]
  IC2 = DIP - 8 pins [chip_label="Relay board" package="DIP (Dual Inline) [THT]"]
  U4 = ENC28J60 [package=ssop28db]

nets:
  N1: Part1.D9_PWM, S2.3
  N2: Part1.D10_PWM/SS, R1.Pin_1, DS2.DQ, DS3.DQ
  N3: Part1.D11_PWM/MOSI, S3.3
  GND: Part1.GND, Part2.GND, U1.GND, DS2.GND, DS3.GND, J1.GND, U3.VSS, U3.PSB, U3.BLK, S2.2, S3.2, IC2.gnd, U4.VSS
  N4: Part1.D0/RX, Part2.D1/TX
  N5: Part1.D1/TX, Part2.D0/RX
  N6: Part1.D2, IC2.io2
  N7: Part1.D3_PWM, IC2.io1
  N8: Part1.D5_PWM, U3.E
  N9: Part1.D6_PWM, U3.CS1
  N10: Part1.D7, U3.R_W
  VDD: Part1.VIN, Part2.VIN, U1.output_voltage, R1.Pin_0, DS2.VDD, DS3.VDD, S1.L1, U3.VDD, U4.VDD
  N11: Part2.D10_PWM/SS, U4.CS
  N12: Part2.D11_PWM/MOSI, U4.SI
  N13: Part2.D12/MISO, U4.SO
  N14: Part2.D13/SCK, U4.SCK
  N15: U1.input_voltage, J1.PWR, IC2.12vin
  N16: S1.L2, U3.BLA

notes:
  12v

custom parts:
  Graphical LCD 128x64: Graphical LCD 128x64 Footprint is not yet proven. Double check it. Spark Fun Electronics SKU : LCD-00710
  DIP - 8 pins: A DIP stand-in part for whatever IC you want. With 8 pins on a 300mil dual inline package (DIP) footprint.
